// Logisim project Versuch1.circ as structural Verilog: 4 circuits, main circuit main
module main (
  input  X0,
  input  X1,
  output out_3
);

  NAND_NMOS nand_nmos_1 (.X1(X0), .X2(X1), .Y(out_3));

  // Notes on the sheet:
  //   Nils Helming
  //   Nabeel Elamaireh
  //   Lukas Piening
  //   27.10.2020
endmodule

module NAND_NMOS (
  input  X1,
  input  X2,
  output Y
);

  wire transistor_2_out;

  Pull_Resistor #(.pull(1)) pull_resistor_1 (.node(Y));
  Transistor #(.\type ("n")) transistor_1 (.in(transistor_2_out), .out(Y), .gate(X1));
  Transistor #(.\type ("n")) transistor_2 (.in(1'b0), .out(transistor_2_out), .gate(X2));

  // Notes on the sheet:
  //   Nils Helming
  //   Nabeel Elamaireh
  //   Lukas Piening
  //   27.10.2020
endmodule

module NAND_CMOS (
  input  X1,
  input  X2,
  output f
);

  wire transistor_4_out;

  Transistor transistor_1 (.in(1'b1), .out(f), .gate(X1));
  Transistor transistor_2 (.in(1'b1), .out(f), .gate(X2));
  Transistor #(.\type ("n")) transistor_3 (.in(transistor_4_out), .out(f), .gate(X1));
  Transistor #(.\type ("n")) transistor_4 (.in(1'b0), .out(transistor_4_out), .gate(X2));

  // Notes on the sheet:
  //   Nils Helming
  //   Nabeel Elamaireh
  //   Lukas Piening
  //   27.10.2020
endmodule

module NOR_CMOS (
  input  X1,
  input  X2,
  output Y
);

  wire transistor_2_out;

  Transistor #(.\type ("n")) transistor_1 (.in(1'b0), .out(Y), .gate(X1));
  Transistor transistor_2 (.in(1'b1), .out(transistor_2_out), .gate(X1));
  Transistor transistor_3 (.in(transistor_2_out), .out(Y), .gate(X2));
  Transistor #(.\type ("n")) transistor_4 (.in(1'b0), .out(Y), .gate(X2));

  // Notes on the sheet:
  //   Nils Helming
  //   Nabeel Elamaireh
  //   Lukas Piening
  //   27.10.2020
endmodule
